# Fritzing sketch diagram (saved by Fritzing 0.9.3b)
breadboards: 1

parts:
  OLED1 = 128x32 I2C Monochrome OLED Display
  S1 = Pushbutton [package="[THT]"]
  R1 = Resistor [tolerance=±5% resistance=10k package=THT]
  J1 = T Cobbler Plus
  YF-S201_Flow_Meter1 = YF-S201 Water Flow Meter

nets:
  N1: OLED1.SDA, J1.SDA
  N2: OLED1.SCL, J1.SCL
  N3: OLED1.RST, J1.#23
  N4: OLED1.GND, R1.Pin_1, J1.GND#24, YF-S201_Flow_Meter1.SIG
  3.3V: OLED1.3.3V, S1.Pin_3, S1.Pin_4, J1.3.3V, YF-S201_Flow_Meter1.VCC
  N5: S1.Pin_1, S1.Pin_2, R1.Pin_0, J1.#16
  N6: J1.#25, YF-S201_Flow_Meter1.GND

custom parts:
  T Cobbler Plus: The T-Cobbler Plus is an add on prototyping board from Adafruit specifically designed for the Raspberry Pi B+ that can break out all those tasty power, GPIO, I2C and SPI pins from the 40-pin header onto a solderless breadboard. This set will make "cobbling together" prototypes with the Pi super easy. The T-Cobbler Plus can plug into any solderless breadboard.
  YF-S201 Water Flow Meter: The YF-S201 Flow Meter. The input voltage is 5V to 24V (DC).
